# Fritzing sketch humidity-sensor (saved by Fritzing 0.9.3b)
breadboards: 1

parts:
  WeMos_D1_Mini1 = WeMos D1 Mini
  RHT1 = Humidity and Temperature Sensor RHT03
  U1 = Battery Holders [package=lipo-1100mAh]
  R1 = Resistor [tolerance=±5% resistance=220 package=THT]
  R2 = Resistor [tolerance=±5% resistance=10k package=THT]
  R3 = Resistor [tolerance=±5% resistance=10k package=THT]
  U2 = SWITCH_SPDT [package=kps-1290]

nets:
  3V3: WeMos_D1_Mini1.3V3, RHT1.Vcc, R1.Pin_0, R3.Pin_1
  N1: WeMos_D1_Mini1.5V, R2.Pin_0, U2.P
  N2: WeMos_D1_Mini1.A0, R2.Pin_1, R3.Pin_0
  N3: WeMos_D1_Mini1.D0, WeMos_D1_Mini1.RST
  N4: WeMos_D1_Mini1.D2, RHT1.Data-signal, R1.Pin_1
  N5: WeMos_D1_Mini1.G, RHT1.GND_2, U1.-
  N6: U1.+, U2.O
